# Fritzing sketch Thermometer-PT100-Fritzing (saved by Fritzing 0.9.3b)
breadboards: 1

parts:
  R1 = Resistor [tolerance=±5% resistance=15k package=THT]
  JP1 = Header 1 [package=1x01_offset]
  JP2 = Header 1 [package=1x01_offset]
  JP3 = Header 1 [package=1x01_offset]
  JP4 = Header 1 [package=1x01_offset]
  IC2 = AD620 - Low Cost Low Power Instrumentation Amplifier [part_number=AD620]
  R4 = Resistor [tolerance=±5% resistance=1.8k package=THT]
  IC3 = TL084 [package=dil14]
  R5 = Resistor [tolerance=±5% resistance=15k package=THT]
  JP6 = Header 1 [package=1x01_offset]
  C1 = Ceramic Capacitor [capacitance=100nF package="100 mil [THT, multilayer]"]
  R10 = Trimmer Potentiometer [maximum_resistance=10kΩ package=THT]
  C3 = Ceramic Capacitor [capacitance=100nF package="100 mil [THT, multilayer]"]
  JP5 = Header 1 [package=1x01_offset]
  R7 = Resistor [tolerance=±5% resistance=15k package=THT]
  R9 = Resistor [tolerance=±5% resistance=15k package=THT]
  R8 = Resistor [tolerance=±5% resistance=15k package=THT]
  C2 = Ceramic Capacitor [capacitance=100nF package="100 mil [THT, multilayer]"]
  R3 = Resistor [tolerance=±5% resistance=5.6k package=THT]  # not connected
  R2 = Resistor [tolerance=±5% resistance=3k package=THT]
  JP7 = Header 1 [package=1x01_offset]
  JP8 = Header 1 [package=1x01_offset]
  R6 = Resistor [tolerance=±5% resistance=1.8k package=THT]

nets (from the schematic view):
  5V: R1.Pin_0, IC2.+VS, IC3.VCC+, R10.leg2, C3.1, R8.Pin_0, R2.Pin_0, JP7.1
  N1: R1.Pin_1, JP4.1, IC3.1IN-
  N2: JP1.1, IC3.1OUT
  N3: JP2.1, IC2.-IN
  N4: JP3.1, IC2.+IN
  GND: IC2.-VS, IC3.VCC-, C1.0, R10.leg1, C3.0, JP5.1, R9.Pin_1, C2.0, JP8.1
  SymGND: IC2.REF, IC3.1IN+, IC3.3OUT, IC3.3IN-
  N5: IC2.OUTPUT, R4.Pin_0
  N6: R4.Pin_1, IC3.2IN+, R5.Pin_0
  N7: IC3.2IN-, R7.Pin_0, R6.Pin_1
  N8: IC3.2OUT, JP6.1, R7.Pin_1
  N9: IC3.3IN+, C1.1, R9.Pin_0
  N10: IC3.4IN+, R10.wiper, C2.1
  URef: IC3.4IN-, IC3.4OUT, R6.Pin_0

notes:
  Ub
  5V
  0V
  Output
  +
  -
  PT100
  1  2  3  4

custom parts:
  TL084: Standard Opeartionsverstärker
